# Fritzing sketch Cooling Fan Controller (saved by Fritzing 1.0.4)
stripboards: 1

parts:
  IC1 = Voltage Regulator [package=78xxl]
  DHT11 = DHT11 Humitidy and Temperature Sensor (3 pins)
  V_Battery = DC Power [voltage=12V internal_resistance=0.1Ω]  # not connected
  Q1 = Basic FET N-Channel [part_number=IRLZ34N package="TO220 [THT]"]
  R2 = Resistor [tolerance=±5% resistance=10k power=0.25W package=THT]
  D1 = Rectifier Diode 800mil [part_number=1N4001 package="800 mil [THT]"]
  R4 = Resistor [tolerance=±5% power=0.25W resistance=10k package=THT]
  DS1 = DS18B20 1-Wire Temperature Sensor [part_number=DS18B20]
  WeMos_D1_Mini1 = WeMos D1 Mini
  R3 = Resistor [tolerance=±5% power=0.25W resistance=10k package=THT]
  R1 = Resistor [tolerance=±5% power=0.25W resistance=220 package=THT]
  JP1 = Header 2 [package=molex-1x2_lock]
  J4 = Camdenboss CTB0158-2 [part_number=CTB0158-2 package=THT]
  JP2 = Header 2 [package=molex-1x2_lock]
  J3 = Camdenboss CTB0158-3 [part_number=CTB0158-3 package=THT]

nets:
  GND: IC1.GND, DHT11.Gnd, Q1.source, R2.Pin_0, WeMos_D1_Mini1.G, J4.pin1, J3.pin1
  12V: IC1.IN, D1.cathode, JP1.1, J4.pin2, JP2.1
  5V: IC1.OUT, DHT11.Plus, R4.Pin_0, WeMos_D1_Mini1.5V, R3.Pin_1, J3.pin3
  N1: DHT11.Signal, WeMos_D1_Mini1.D4, R3.Pin_0
  N2: Q1.gate, R2.Pin_1, R1.Pin_0
  N3: Q1.drain, D1.anode, JP1.2, JP2.2
  N4: R4.Pin_1, WeMos_D1_Mini1.D3, J3.pin2
  N5: DS1.GND, J3.terminal_1
  N6: DS1.DQ, J3.terminal_2
  N7: DS1.VDD, J3.terminal_3
  N8: WeMos_D1_Mini1.D2, R1.Pin_1

notes:
  12V to 5V Buck Converter
  Ambient Temperature Sensor
  Charger Temperature Sensor
  Fan Speed Driver
  The Brain

custom parts:
  DHT11 Humitidy and Temperature Sensor (3 pins): DHT11 Humidity and Temperature Sensor (3 pins).
  Rectifier Diode 800mil: A standard rectifier diode streched to 800mil
